// Logisim project 8-bit-computer.circ as structural Verilog: 1 circuit, main circuit main
module main (
  input  PC_in,
  input  PC_write,
  input  IR_in,
  input  MEM_out,
  input  in_5,
  input  in_6,
  input  in_7,
  input  in_8,
  input  in_9,
  input  in_10,
  input  in_11,
  input  in_12,
  input  OUT_in,
  input  Signed,
  input  MAR_in,
  input  RAM_out,
  input  RAM_in,
  input  A_in,
  input  A_out,
  input  B_in,
  input  B_out,
  input  ALU_out,
  input  ALU_op,
  input  in_24,
  output out_25,
  output out_26,
  output out_27,
  output out_28,
  output out_29,
  output out_30,
  output out_31,
  output out_32
);

  wire and_1_out, and_2_out, and_3_out, and_4_out, and_5_out, and_6_out, and_7_out, and_8_out, and_9_out,
       and_10_out, and_11_out, and_12_out, and_13_out, and_14_out, and_15_out, and_16_out, and_17_out,
       and_18_out, and_19_out, and_20_out, and_21_out, and_22_out, and_23_out, and_24_out, and_25_out,
       and_26_out, and_27_out, and_28_out, and_29_out, and_30_out, and_31_out, and_32_out, and_33_out,
       and_34_out, and_35_out, and_36_out, and_37_out, and_38_out, and_39_out, and_40_out, and_41_out,
       and_42_out, and_43_out, and_44_out, and_45_out, and_46_out, and_47_out, and_48_out, and_49_out,
       and_50_out, and_51_out, and_52_out, and_53_out, and_54_out, and_55_out, and_56_out, and_57_out,
       and_58_out, and_59_out, and_60_out, and_61_out, and_62_out, and_63_out, and_64_out, and_65_out,
       and_66_out, and_67_out, and_68_out, and_69_out, and_70_out, and_71_out, and_72_out, and_73_out,
       and_74_out, and_75_out, and_76_out, and_77_out, and_78_out, and_79_out, and_80_out, and_81_out,
       and_82_out, and_83_out, and_84_out, and_85_out, and_86_out, and_87_out, and_88_out, and_89_out,
       and_90_out, and_91_out, and_92_out, and_93_out, and_94_out, and_95_out, and_96_out, and_97_out,
       and_98_out, and_99_out, and_100_out, Clock_out, not_1_out, not_2_out, not_3_out, not_4_out, not_5_out,
       not_6_out, not_7_out, not_8_out, not_9_out, not_10_out, not_11_out, not_12_out, not_13_out,
       not_14_out, or_1_out, or_3_out, or_5_out, or_7_out, or_9_out, or_11_out, or_13_out, or_15_out,
       or_17_out, or_18_out, or_19_out, or_20_out, or_21_out, or_22_out, or_23_out, or_24_out, or_25_out,
       or_26_out, or_27_out, or_28_out, or_29_out, or_30_out, or_31_out, or_32_out, or_33_out, or_34_out,
       or_35_out, or_36_out, or_37_out, or_38_out, or_39_out, or_40_out, or_41_out, or_42_out, or_43_out,
       or_44_out, or_45_out, or_46_out, or_47_out, or_48_out, or_49_out, or_50_out, or_51_out, or_52_out,
       or_53_out, or_54_out, or_55_out, or_56_out, or_57_out, or_58_out, or_59_out, or_60_out, or_61_out,
       or_62_out, or_63_out, or_64_out, or_65_out, or_66_out, or_67_out, or_68_out, or_69_out, or_70_out,
       or_71_out, or_72_out, register_21_q, register_22_q, register_23_q, register_24_q, register_25_q,
       register_26_q, register_27_q, register_28_q, register_29_q, register_30_q, register_31_q,
       register_32_q, register_33_q, register_34_q, register_35_q, register_36_q, xor_1_out, xor_2_out,
       xor_3_out, xor_4_out, xor_5_out, xor_6_out, xor_7_out, xor_8_out, xor_9_out, xor_10_out;
  wire [7:0] ram_1_data, register_13_q, register_37_q, register_45_q, rom_1_data, rom_2_data, rom_3_data,
       rom_4_data, rom_5_data, rom_6_data, rom_7_data, rom_8_data;
  wire [11:0] register_1_q;

  not not_1 (not_1_out, Clock_out);
  Clock Clock (.out(Clock_out));
  Register #(.width(1)) register_1 (.D(not_3_out), .en(1'b1), .Q(register_1_q[0]), .clk(Clock_out));  // open: clr
  Register #(.width(1)) register_2 (.D(xor_1_out), .en(1'b1), .Q(register_1_q[1]), .clk(Clock_out));  // open: clr
  Register #(.width(1)) register_3 (.D(xor_2_out), .en(1'b1), .Q(register_1_q[2]), .clk(Clock_out));  // open: clr
  Register #(.width(1)) register_4 (.D(xor_3_out), .en(1'b1), .Q(register_1_q[3]), .clk(Clock_out));  // open: clr
  not not_2 (not_2_out, Clock_out);
  Register #(.width(1)) register_5 (.D(out_32), .en(IR_in), .Q(register_1_q[4]), .clk(not_2_out));  // open: clr
  Register #(.width(1)) register_6 (.D(out_31), .en(IR_in), .Q(register_1_q[5]), .clk(not_2_out));  // open: clr
  Register #(.width(1)) register_7 (.D(out_30), .en(IR_in), .Q(register_1_q[6]), .clk(not_2_out));  // open: clr
  Register #(.width(1)) register_8 (.D(out_29), .en(IR_in), .Q(register_1_q[7]), .clk(not_2_out));  // open: clr
  Register #(.width(1)) register_9 (.D(out_28), .en(IR_in), .Q(register_1_q[8]), .clk(not_2_out));  // open: clr
  Register #(.width(1)) register_10 (.D(out_27), .en(IR_in), .Q(register_1_q[9]), .clk(not_2_out));  // open: clr
  Register #(.width(1)) register_11 (.D(out_26), .en(IR_in), .Q(register_1_q[10]), .clk(not_2_out));  // open: clr
  Register #(.width(1)) register_12 (.D(out_25), .en(IR_in), .Q(register_1_q[11]), .clk(not_2_out));  // open: clr
  not not_3 (not_3_out, register_1_q[0]);
  and and_1 (and_1_out, register_1_q[0], register_1_q[1]);
  and and_2 (and_2_out, and_1_out, register_1_q[2]);
  xor xor_1 (xor_1_out, register_1_q[0], register_1_q[1]);
  xor xor_2 (xor_2_out, and_1_out, register_1_q[2]);
  xor xor_3 (xor_3_out, and_2_out, register_1_q[3]);
  ROM #(.addrWidth(14)) rom_1 (.addr({2'b00, register_1_q}), .data(rom_1_data));  // open: sel
  ROM #(.addrWidth(14)) rom_2 (.addr({2'b01, register_1_q}), .data(rom_2_data));  // open: sel
  ROM #(.addrWidth(14)) rom_3 (.addr({2'b10, register_1_q}), .data(rom_3_data));  // open: sel
  ROM #(.addrWidth(14)) rom_4 (.addr({2'b11, register_1_q}), .data(rom_4_data));  // open: sel
  or or_1 (or_1_out, or_17_out, or_18_out);
  or or_2 (out_32, or_1_out, or_19_out);
  or or_3 (or_3_out, or_20_out, or_21_out);
  or or_4 (out_31, or_3_out, or_22_out);
  or or_5 (or_5_out, or_23_out, or_24_out);
  or or_6 (out_30, or_5_out, or_25_out);
  or or_7 (or_7_out, or_26_out, or_27_out);
  or or_8 (out_29, or_7_out, or_28_out);
  or or_9 (or_9_out, or_29_out, or_30_out);
  or or_10 (out_28, or_9_out, or_31_out);
  or or_11 (or_11_out, or_32_out, or_33_out);
  or or_12 (out_27, or_11_out, or_34_out);
  or or_13 (or_13_out, or_35_out, or_36_out);
  or or_14 (out_26, or_13_out, or_37_out);
  or or_15 (or_15_out, or_38_out, or_39_out);
  or or_16 (out_25, or_15_out, or_40_out);
  Register #(.width(1)) register_13 (.D(out_32), .en(MAR_in), .Q(register_13_q[0]), .clk(not_1_out));  // open: clr
  Register #(.width(1)) register_14 (.D(out_31), .en(MAR_in), .Q(register_13_q[1]), .clk(not_1_out));  // open: clr
  Register #(.width(1)) register_15 (.D(out_30), .en(MAR_in), .Q(register_13_q[2]), .clk(not_1_out));  // open: clr
  Register #(.width(1)) register_16 (.D(out_29), .en(MAR_in), .Q(register_13_q[3]), .clk(not_1_out));  // open: clr
  Register #(.width(1)) register_17 (.D(out_28), .en(MAR_in), .Q(register_13_q[4]), .clk(not_1_out));  // open: clr
  Register #(.width(1)) register_18 (.D(out_27), .en(MAR_in), .Q(register_13_q[5]), .clk(not_1_out));  // open: clr
  Register #(.width(1)) register_19 (.D(out_26), .en(MAR_in), .Q(register_13_q[6]), .clk(not_1_out));  // open: clr
  Register #(.width(1)) register_20 (.D(out_25), .en(MAR_in), .Q(register_13_q[7]), .clk(not_1_out));  // open: clr
  Register #(.width(1)) register_21 (.D(out_32), .en(A_in), .Q(register_21_q), .clk(not_1_out));  // open: clr
  Register #(.width(1)) register_22 (.D(out_31), .en(A_in), .Q(register_22_q), .clk(not_1_out));  // open: clr
  Register #(.width(1)) register_23 (.D(out_30), .en(A_in), .Q(register_23_q), .clk(not_1_out));  // open: clr
  Register #(.width(1)) register_24 (.D(out_29), .en(A_in), .Q(register_24_q), .clk(not_1_out));  // open: clr
  Register #(.width(1)) register_25 (.D(out_28), .en(A_in), .Q(register_25_q), .clk(not_1_out));  // open: clr
  Register #(.width(1)) register_26 (.D(out_27), .en(A_in), .Q(register_26_q), .clk(not_1_out));  // open: clr
  Register #(.width(1)) register_27 (.D(out_26), .en(A_in), .Q(register_27_q), .clk(not_1_out));  // open: clr
  Register #(.width(1)) register_28 (.D(out_25), .en(A_in), .Q(register_28_q), .clk(not_1_out));  // open: clr
  Register #(.width(1)) register_29 (.D(out_32), .en(B_in), .Q(register_29_q), .clk(not_1_out));  // open: clr
  Register #(.width(1)) register_30 (.D(out_31), .en(B_in), .Q(register_30_q), .clk(not_1_out));  // open: clr
  Register #(.width(1)) register_31 (.D(out_30), .en(B_in), .Q(register_31_q), .clk(not_1_out));  // open: clr
  Register #(.width(1)) register_32 (.D(out_29), .en(B_in), .Q(register_32_q), .clk(not_1_out));  // open: clr
  Register #(.width(1)) register_33 (.D(out_28), .en(B_in), .Q(register_33_q), .clk(not_1_out));  // open: clr
  Register #(.width(1)) register_34 (.D(out_27), .en(B_in), .Q(register_34_q), .clk(not_1_out));  // open: clr
  Register #(.width(1)) register_35 (.D(out_26), .en(B_in), .Q(register_35_q), .clk(not_1_out));  // open: clr
  Register #(.width(1)) register_36 (.D(out_25), .en(B_in), .Q(register_36_q), .clk(not_1_out));  // open: clr
  or or_17 (or_17_out, and_68_out, and_3_out);
  or or_18 (or_18_out, and_11_out, and_19_out);
  or or_19 (or_19_out, and_32_out, in_12);
  or or_20 (or_20_out, and_69_out, and_4_out);
  or or_21 (or_21_out, and_12_out, and_20_out);
  or or_22 (or_22_out, and_37_out, in_11);
  or or_23 (or_23_out, and_70_out, and_5_out);
  or or_24 (or_24_out, and_13_out, and_21_out);
  or or_25 (or_25_out, and_42_out, in_10);
  or or_26 (or_26_out, and_71_out, and_6_out);
  or or_27 (or_27_out, and_14_out, and_22_out);
  or or_28 (or_28_out, and_47_out, in_9);
  or or_29 (or_29_out, and_72_out, and_7_out);
  or or_30 (or_30_out, and_15_out, and_23_out);
  or or_31 (or_31_out, and_76_out, in_8);
  or or_32 (or_32_out, and_73_out, and_8_out);
  or or_33 (or_33_out, and_16_out, and_24_out);
  or or_34 (or_34_out, and_87_out, in_7);
  or or_35 (or_35_out, and_74_out, and_9_out);
  or or_36 (or_36_out, and_17_out, and_25_out);
  or or_37 (or_37_out, and_92_out, in_6);
  or or_38 (or_38_out, and_75_out, and_10_out);
  or or_39 (or_39_out, and_18_out, and_26_out);
  or or_40 (or_40_out, and_97_out, in_5);
  RAM #(.bus("separate")) ram_1 (
    .addr(register_13_q), .din({out_25, out_26, out_27, out_28, out_29, out_30, out_31, out_32}),
    .data(ram_1_data), .str(RAM_in), .clk(not_1_out));  // open: sel, ld, clr
  not not_4 (not_4_out, ALU_op);
  not not_5 (not_5_out, in_24);
  and and_3 (and_3_out, ram_1_data[0], RAM_out);
  and and_4 (and_4_out, ram_1_data[1], RAM_out);
  and and_5 (and_5_out, ram_1_data[2], RAM_out);
  and and_6 (and_6_out, ram_1_data[3], RAM_out);
  and and_7 (and_7_out, ram_1_data[4], RAM_out);
  and and_8 (and_8_out, ram_1_data[5], RAM_out);
  buf and_9 (and_9_out, ram_1_data[6]);  // AND_Gate
  and and_10 (and_10_out, ram_1_data[7], RAM_out);
  and and_11 (and_11_out, register_21_q, A_out);
  and and_12 (and_12_out, register_22_q, A_out);
  and and_13 (and_13_out, register_23_q, A_out);
  and and_14 (and_14_out, register_24_q, A_out);
  and and_15 (and_15_out, register_25_q, A_out);
  and and_16 (and_16_out, register_26_q, A_out);
  and and_17 (and_17_out, register_27_q, A_out);
  and and_18 (and_18_out, register_28_q, A_out);
  and and_19 (and_19_out, register_29_q, B_out);
  and and_20 (and_20_out, register_30_q, B_out);
  and and_21 (and_21_out, register_31_q, B_out);
  and and_22 (and_22_out, register_32_q, B_out);
  and and_23 (and_23_out, register_33_q, B_out);
  and and_24 (and_24_out, register_34_q, B_out);
  and and_25 (and_25_out, register_35_q, B_out);
  and and_26 (and_26_out, register_36_q, B_out);
  and and_27 (and_27_out, and_28_out, 1'b0);
  and and_28 (and_28_out, not_5_out, not_4_out);
  and and_29 (and_29_out, in_24, not_4_out);
  and and_30 (and_30_out, not_5_out, ALU_op);
  and and_31 (and_31_out, in_24, ALU_op);
  and and_32 (and_32_out, or_41_out, ALU_out);
  or or_41 (or_41_out, or_42_out, or_43_out);
  or or_42 (or_42_out, and_27_out, and_34_out);
  and and_33 (and_33_out, and_30_out, 1'b0);
  and and_34 (and_34_out, and_29_out, 1'b0);
  or or_43 (or_43_out, and_33_out, and_36_out);
  and and_35 (and_35_out, and_28_out, 1'b0);
  and and_36 (and_36_out, and_31_out, 1'b0);
  and and_37 (and_37_out, or_44_out, ALU_out);
  or or_44 (or_44_out, or_45_out, or_46_out);
  or or_45 (or_45_out, and_35_out, and_38_out);
  and and_38 (and_38_out, and_29_out, 1'b0);
  and and_39 (and_39_out, and_30_out, 1'b0);
  or or_46 (or_46_out, and_39_out, and_41_out);
  and and_40 (and_40_out, and_28_out, 1'b0);
  and and_41 (and_41_out, and_31_out, 1'b0);
  and and_42 (and_42_out, or_47_out, ALU_out);
  or or_47 (or_47_out, or_48_out, or_49_out);
  or or_48 (or_48_out, and_40_out, and_44_out);
  and and_43 (and_43_out, and_30_out, 1'b0);
  and and_44 (and_44_out, and_29_out, 1'b0);
  or or_49 (or_49_out, and_43_out, and_46_out);
  and and_45 (and_45_out, and_28_out, 1'b0);
  and and_46 (and_46_out, and_31_out, 1'b0);
  Register #(.width(1)) register_37 (.D(out_32), .en(OUT_in), .Q(register_37_q[0]), .clk(not_1_out));  // open: clr
  Register #(.width(1)) register_38 (.D(out_31), .en(OUT_in), .Q(register_37_q[1]), .clk(not_1_out));  // open: clr
  Register #(.width(1)) register_39 (.D(out_30), .en(OUT_in), .Q(register_37_q[2]), .clk(not_1_out));  // open: clr
  Register #(.width(1)) register_40 (.D(out_29), .en(OUT_in), .Q(register_37_q[3]), .clk(not_1_out));  // open: clr
  Register #(.width(1)) register_41 (.D(out_28), .en(OUT_in), .Q(register_37_q[4]), .clk(not_1_out));  // open: clr
  Register #(.width(1)) register_42 (.D(out_27), .en(OUT_in), .Q(register_37_q[5]), .clk(not_1_out));  // open: clr
  Register #(.width(1)) register_43 (.D(out_26), .en(OUT_in), .Q(register_37_q[6]), .clk(not_1_out));  // open: clr
  Register #(.width(1)) register_44 (.D(out_25), .en(OUT_in), .Q(register_37_q[7]), .clk(not_1_out));  // open: clr
  and and_47 (and_47_out, or_50_out, ALU_out);
  or or_50 (or_50_out, or_51_out, or_52_out);
  or or_51 (or_51_out, and_45_out, and_48_out);
  and and_48 (and_48_out, and_29_out, 1'b0);
  and and_49 (and_49_out, and_30_out, 1'b0);
  not not_6 (not_6_out, PC_write);
  not not_7 (not_7_out, PC_write);
  not not_8 (not_8_out, PC_write);
  not not_9 (not_9_out, PC_write);
  not not_10 (not_10_out, PC_write);
  not not_11 (not_11_out, PC_write);
  not not_12 (not_12_out, PC_write);
  not not_13 (not_13_out, PC_write);
  or or_52 (or_52_out, and_49_out, and_50_out);
  and and_50 (and_50_out, and_31_out, 1'b0);
  and and_51 (and_51_out, and_28_out, 1'b0);
  and and_52 (and_52_out, not_14_out, not_6_out);
  or or_53 (or_53_out, and_52_out, and_53_out);
  and and_53 (and_53_out, PC_write, out_32);
  and and_54 (and_54_out, xor_4_out, not_7_out);
  or or_54 (or_54_out, and_54_out, and_55_out);
  and and_55 (and_55_out, PC_write, out_31);
  and and_56 (and_56_out, xor_5_out, not_8_out);
  or or_55 (or_55_out, and_56_out, and_57_out);
  and and_57 (and_57_out, PC_write, out_30);
  and and_58 (and_58_out, xor_6_out, not_9_out);
  or or_56 (or_56_out, and_58_out, and_59_out);
  and and_59 (and_59_out, PC_write, out_29);
  and and_60 (and_60_out, xor_7_out, not_10_out);
  or or_57 (or_57_out, and_60_out, and_61_out);
  and and_61 (and_61_out, PC_write, out_28);
  and and_62 (and_62_out, xor_8_out, not_11_out);
  or or_58 (or_58_out, and_62_out, and_63_out);
  and and_63 (and_63_out, PC_write, out_27);
  and and_64 (and_64_out, xor_9_out, not_12_out);
  or or_59 (or_59_out, and_64_out, and_65_out);
  and and_65 (and_65_out, PC_write, out_26);
  and and_66 (and_66_out, xor_10_out, not_13_out);
  or or_60 (or_60_out, and_66_out, and_67_out);
  and and_67 (and_67_out, PC_write, out_25);
  ROM rom_5 (.addr(register_45_q), .data(rom_5_data));  // open: sel
  and and_68 (and_68_out, MEM_out, rom_5_data[0]);
  and and_69 (and_69_out, MEM_out, rom_5_data[1]);
  and and_70 (and_70_out, MEM_out, rom_5_data[2]);
  and and_71 (and_71_out, MEM_out, rom_5_data[3]);
  and and_72 (and_72_out, MEM_out, rom_5_data[4]);
  and and_73 (and_73_out, MEM_out, rom_5_data[5]);
  and and_74 (and_74_out, MEM_out, rom_5_data[6]);
  and and_75 (and_75_out, MEM_out, rom_5_data[7]);
  and and_76 (and_76_out, or_61_out, ALU_out);
  or or_61 (or_61_out, or_62_out, or_63_out);
  or or_62 (or_62_out, and_51_out, and_78_out);
  and and_77 (and_77_out, and_30_out, 1'b0);
  and and_78 (and_78_out, and_29_out, 1'b0);
  Register #(.width(1)) register_45 (.D(or_53_out), .en(PC_in), .Q(register_45_q[0]), .clk(not_1_out));  // open: clr
  Register #(.width(1)) register_46 (.D(or_54_out), .en(PC_in), .Q(register_45_q[1]), .clk(not_1_out));  // open: clr
  Register #(.width(1)) register_47 (.D(or_55_out), .en(PC_in), .Q(register_45_q[2]), .clk(not_1_out));  // open: clr
  Register #(.width(1)) register_48 (.D(or_56_out), .en(PC_in), .Q(register_45_q[3]), .clk(not_1_out));  // open: clr
  Register #(.width(1)) register_49 (.D(or_57_out), .en(PC_in), .Q(register_45_q[4]), .clk(not_1_out));  // open: clr
  Register #(.width(1)) register_50 (.D(or_58_out), .en(PC_in), .Q(register_45_q[5]), .clk(not_1_out));  // open: clr
  Register #(.width(1)) register_51 (.D(or_59_out), .en(PC_in), .Q(register_45_q[6]), .clk(not_1_out));  // open: clr
  Register #(.width(1)) register_52 (.D(or_60_out), .en(PC_in), .Q(register_45_q[7]), .clk(not_1_out));  // open: clr
  ROM #(.addrWidth(9)) rom_6 (.addr({Signed, register_37_q}), .data(rom_6_data));  // open: sel
  ROM #(.addrWidth(9)) rom_7 (.addr({Signed, register_37_q}), .data(rom_7_data));  // open: sel
  ROM #(.addrWidth(9)) rom_8 (.addr({Signed, register_37_q}), .data(rom_8_data));  // open: sel
  or or_63 (or_63_out, and_77_out, and_79_out);
  and and_79 (and_79_out, and_31_out, 1'b0);
  and and_80 (and_80_out, and_28_out, 1'b0);
  not not_14 (not_14_out, register_45_q[0]);
  xor xor_4 (xor_4_out, register_45_q[0], register_45_q[1]);
  and and_81 (and_81_out, register_45_q[0], register_45_q[1]);
  xor xor_5 (xor_5_out, and_81_out, register_45_q[2]);
  and and_82 (and_82_out, and_81_out, register_45_q[2]);
  xor xor_6 (xor_6_out, and_82_out, register_45_q[3]);
  and and_83 (and_83_out, and_82_out, register_45_q[3]);
  xor xor_7 (xor_7_out, and_83_out, register_45_q[4]);
  and and_84 (and_84_out, and_83_out, register_45_q[4]);
  xor xor_8 (xor_8_out, and_84_out, register_45_q[5]);
  and and_85 (and_85_out, and_84_out, register_45_q[5]);
  xor xor_9 (xor_9_out, and_85_out, register_45_q[6]);
  and and_86 (and_86_out, and_85_out, register_45_q[6]);
  xor xor_10 (xor_10_out, and_86_out, register_45_q[7]);
  DotMatrix #(.matrixcols(3), .matrixrows(1)) dotmatrix_1 (
    .col0(rom_6_data[7]), .col1(rom_6_data[7]), .col2(rom_6_data[7]));
  and and_87 (and_87_out, or_64_out, ALU_out);
  or or_64 (or_64_out, or_65_out, or_66_out);
  or or_65 (or_65_out, and_80_out, and_89_out);
  and and_88 (and_88_out, and_30_out, 1'b0);
  and and_89 (and_89_out, and_29_out, 1'b0);
  _7_Segment_Display u_7_segment_display_1 (
    .g(rom_7_data[3]), .f(rom_7_data[2]), .a(rom_7_data[1]), .b(rom_7_data[0]), .e(rom_7_data[4]),
    .d(rom_7_data[5]), .c(rom_7_data[6]));  // open: dp
  _7_Segment_Display u_7_segment_display_2 (
    .g(rom_6_data[3]), .f(rom_6_data[2]), .a(rom_6_data[1]), .b(rom_6_data[0]), .e(rom_6_data[4]),
    .d(rom_6_data[5]), .c(rom_6_data[6]));  // open: dp
  or or_66 (or_66_out, and_88_out, and_90_out);
  and and_90 (and_90_out, and_31_out, 1'b0);
  and and_91 (and_91_out, and_28_out, 1'b0);
  _7_Segment_Display u_7_segment_display_3 (
    .g(rom_8_data[3]), .f(rom_8_data[2]), .a(rom_8_data[1]), .b(rom_8_data[0]), .e(rom_8_data[4]),
    .d(rom_8_data[5]), .c(rom_8_data[6]));  // open: dp
  and and_92 (and_92_out, or_67_out, ALU_out);
  or or_67 (or_67_out, or_68_out, or_69_out);
  or or_68 (or_68_out, and_91_out, and_94_out);
  and and_93 (and_93_out, and_30_out, 1'b0);
  and and_94 (and_94_out, and_29_out, 1'b0);
  or or_69 (or_69_out, and_93_out, and_95_out);
  and and_95 (and_95_out, and_31_out, 1'b0);
  and and_96 (and_96_out, and_28_out, 1'b0);
  and and_97 (and_97_out, or_70_out, ALU_out);
  or or_70 (or_70_out, or_71_out, or_72_out);
  or or_71 (or_71_out, and_96_out, and_98_out);
  and and_98 (and_98_out, and_29_out, 1'b0);
  and and_99 (and_99_out, and_30_out, 1'b0);
  or or_72 (or_72_out, and_99_out, and_100_out);
  and and_100 (and_100_out, and_31_out, 1'b0);

  // Notes on the sheet:
  //   MAR
  //   Manual Bus Override
  //   contents of rom_6 (hex, n*v repeats v):
  //   100*77 100*41 56*3b 100*77 28*41 29*c1 99*f7
  //   contents of rom_7 (hex, n*v repeats v):
  //   10*77 10*41 10*3b 10*6b 10*4d 10*6e 10*7e 10*43 10*7f 10*6f 10*77 10*41 10*3b 10*6b 10*4d 10*6e
  //   10*7e 10*43 10*7f 10*6f 10*77 10*41 10*3b 10*6b 10*4d 6*6e 10*77 10*41 10*3b 10*6b 10*4d 10*6e 10*7e
  //   10*43 10*7f 10*6f 10*77 10*41 17*3b 10*41 10*77 10*6f 10*7f 10*43 10*7e 10*6e 10*4d 10*6b 10*3b
  //   10*41 9*77
  //   contents of rom_8 (hex, n*v repeats v):
  //   77 41 3b 6b 4d 6e 7e 43 7f 6f 77 41 3b 6b 4d 6e 7e 43 7f 6f 77 41 3b 6b 4d 6e 7e 43 7f 6f 77 41 3b
  //   6b 4d 6e 7e 43 7f 6f 77 41 3b 6b 4d 6e 7e 43 7f 6f 77 41 3b 6b 4d 6e 7e 43 7f 6f 77 41 3b 6b 4d 6e
  //   7e 43 7f 6f 77 41 3b 6b 4d 6e 7e 43 7f 6f 77 41 3b 6b 4d 6e 7e 43 7f 6f 77 41 3b 6b 4d 6e 7e 43 7f
  //   6f 77 41 3b 6b 4d 6e 7e 43 7f 6f 77 41 3b 6b 4d 6e 7e 43 7f 6f 77 41 3b 6b 4d 6e 7e 43 7f 6f 77 41
  //   3b 6b 4d 6e 7e 43 7f 6f 77 41 3b 6b 4d 6e 7e 43 7f 6f 77 41 3b 6b 4d 6e 7e 43 7f 6f 77 41 3b 6b 4d
  //   6e 7e 43 7f 6f 77 41 3b 6b 4d 6e 7e 43 7f 6f 77 41 3b 6b 4d 6e 7e 43 7f 6f 77 41 3b 6b 4d 6e 7e 43
  //   7f 6f 77 41 3b 6b 4d 6e 7e 43 7f 6f 77 41 3b 6b 4d 6e 7e 43 7f 6f 77 41 3b 6b 4d 6e 7e 43 7f 6f 77
  //   41 3b 6b 4d 6e 7e 43 7f 6f 77 41 3b 6b 4d 6e 7e 43 7f 6f 77 41 3b 6b 4d 6e 77 41 3b 6b 4d 6e 7e 43
  //   7f 6f 77 41 3b 6b 4d 6e 7e 43 7f 6f 77 41 3b 6b 4d 6e 7e 43 7f 6f 77 41 3b 6b 4d 6e 7e 43 7f 6f 77
  //   41 3b 6b 4d 6e 7e 43 7f 6f 77 41 3b 6b 4d 6e 7e 43 7f 6f 77 41 3b 6b 4d 6e 7e 43 7f 6f 77 41 3b 6b
  //   4d 6e 7e 43 7f 6f 77 41 3b 6b 4d 6e 7e 43 7f 6f 77 41 3b 6b 4d 6e 7e 43 7f 6f 77 41 3b 6b 4d 6e 7e
  //   43 7f 6f 77 41 3b 6b 4d 6e 7e 43 7f 6f 77 41 3b 6b 4d 6e 7e 43 7f 43 7e 6e 4d 6b 3b 41 77 6f 7f 43
  //   7e 6e 4d 6b 3b 41 77 6f 7f 43 7e 6e 4d 6b 3b 41 77 6f 7f 43 7e 6e 4d 6b 3b 41 77 6f 7f 43 7e 6e 4d
  //   6b 3b 41 77 6f 7f 43 7e 6e 4d 6b 3b 41 77 6f 7f 43 7e 6e 4d 6b 3b 41 77 6f 7f 43 7e 6e 4d 6b 3b 41
  //   77 6f 7f 43 7e 6e 4d 6b 3b 41 77 6f 7f 43 7e 6e 4d 6b 3b 41 77 6f 7f 43 7e 6e 4d 6b 3b 41 77 6f 7f
  //   43 7e 6e 4d 6b 3b 41 77 6f 7f 43 7e 6e 4d 6b 3b 41
endmodule
